// Logisim project LED_matrix_multiplexer.circ as structural Verilog: 1 circuit, main circuit main
module main (
  input  [31:0] Row_0,
  input  [31:0] Row_1,
  input  [31:0] Row_2,
  input  [31:0] Row_3,
  input  [31:0] Row_4,
  input  [31:0] Row_5,
  input  [31:0] Row_6,
  input  [31:0] Row_7
);

  wire bitselector_2_out, bitselector_3_out, bitselector_4_out, bitselector_5_out, bitselector_6_out,
       bitselector_7_out, bitselector_8_out, bitselector_9_out, CLK, multiplexer_1_out, not_1_out, PLoad,
       shift_register_1_out, shift_register_1_q0, shift_register_1_q1, shift_register_1_q2,
       shift_register_1_q3, shift_register_1_q4, shift_register_1_q5, shift_register_1_q6,
       shift_register_1_q7, shift_register_3_out, shift_register_3_q0, shift_register_3_q1,
       shift_register_3_q2, shift_register_3_q3, shift_register_3_q4, shift_register_3_q5,
       shift_register_3_q6, shift_register_3_q7, shift_register_5_out, shift_register_5_q0,
       shift_register_5_q1, shift_register_5_q2, shift_register_5_q3, shift_register_5_q4,
       shift_register_5_q5, shift_register_5_q6, shift_register_5_q7, shift_register_7_q0,
       shift_register_7_q1, shift_register_7_q2, shift_register_7_q3, shift_register_7_q4,
       shift_register_7_q5, shift_register_7_q6, shift_register_7_q7;
  wire [2:0] counter_1_q, counter_2_q;
  wire [4:0] Bit_Select;
  wire [7:0] decoder_1_out0, dotmatrix_1_p2, rom_2_data, Row_Select, shift_register_2_q7,
       shift_register_4_q7, shift_register_6_q7, shift_register_8_q7;
  wire [7:6] counter_3_q;

  Clock clock_1 (.out(CLK));
  Counter #(.width(3), .max('h7)) counter_1 (
    .D(3'b000), .count(CLK), .Q(counter_1_q), .clk(CLK));  // open: load, carry, clr
  Decoder #(.select(3), .enable("false")) decoder_1 (
    .out0(decoder_1_out0[0]), .out1(decoder_1_out0[1]), .out2(decoder_1_out0[2]), .out3(decoder_1_out0[3]),
    .out4(decoder_1_out0[4]), .out5(decoder_1_out0[5]), .out6(decoder_1_out0[6]), .out7(decoder_1_out0[7]),
    .sel(counter_1_q));
  // DotMatrix #(.inputtype("select"), .matrixcols(8), .matrixrows(8)) dotmatrix_1: pin names not known; wires that end beside it: decoder_1_out0, dotmatrix_1_p2
  ROM #(.addrWidth(3)) rom_1 (.addr(counter_1_q), .data(dotmatrix_1_p2));  // open: sel
  ROM #(.addrWidth(5)) rom_2 (.data(rom_2_data));  // open: addr, sel
  BitSelector bitselector_1 (.in(rom_2_data), .sel(Bit_Select[2:0]));  // open: out
  BitSelector #(.width(32)) bitselector_2 (.in(Row_0), .out(bitselector_2_out), .sel(Bit_Select));
  BitSelector #(.width(32)) bitselector_3 (.in(Row_1), .out(bitselector_3_out), .sel(Bit_Select));
  BitSelector #(.width(32)) bitselector_4 (.in(Row_2), .out(bitselector_4_out), .sel(Bit_Select));
  BitSelector #(.width(32)) bitselector_5 (.in(Row_3), .out(bitselector_5_out), .sel(Bit_Select));
  BitSelector #(.width(32)) bitselector_6 (.in(Row_4), .out(bitselector_6_out), .sel(Bit_Select));
  BitSelector #(.width(32)) bitselector_7 (.in(Row_5), .out(bitselector_7_out), .sel(Bit_Select));
  BitSelector #(.width(32)) bitselector_8 (.in(Row_6), .out(bitselector_8_out), .sel(Bit_Select));
  BitSelector #(.width(32)) bitselector_9 (.in(Row_7), .out(bitselector_9_out), .sel(Bit_Select));
  Counter #(.width(3), .max('h7)) counter_2 (.count(PLoad), .Q(counter_2_q), .clk(CLK));  // open: load, D, carry, clr
  Multiplexer #(.select(3), .disabled(0), .enable("false")) multiplexer_1 (
    .in0(bitselector_2_out), .in1(bitselector_3_out), .in2(bitselector_4_out), .in3(bitselector_5_out),
    .in4(bitselector_6_out), .in5(bitselector_7_out), .in6(bitselector_8_out), .in7(bitselector_9_out),
    .out(multiplexer_1_out), .sel(counter_2_q));
  Decoder #(.select(3), .enable("false")) decoder_2 (
    .out0(Row_Select[7]), .out1(Row_Select[0]), .out2(Row_Select[1]), .out3(Row_Select[2]),
    .out4(Row_Select[3]), .out5(Row_Select[4]), .out6(Row_Select[5]), .out7(Row_Select[6]), .sel(counter_2_q));
  Shift_Register shift_register_1 (
    .in(multiplexer_1_out), .clk(CLK), .out(shift_register_1_out), .q0(shift_register_1_q0),
    .q1(shift_register_1_q1), .q2(shift_register_1_q2), .q3(shift_register_1_q3), .q4(shift_register_1_q4),
    .q5(shift_register_1_q5), .q6(shift_register_1_q6), .q7(shift_register_1_q7));  // open: shift, load, clr, d0, d1, d2, d3, d4, d5, d6, d7
  Shift_Register shift_register_2 (
    .shift(1'b0), .clk(CLK), .load(PLoad), .d0(shift_register_1_q0), .q0(shift_register_2_q7[7]),
    .d1(shift_register_1_q1), .q1(shift_register_2_q7[6]), .d2(shift_register_1_q2),
    .q2(shift_register_2_q7[5]), .d3(shift_register_1_q3), .q3(shift_register_2_q7[4]),
    .d4(shift_register_1_q4), .q4(shift_register_2_q7[3]), .d5(shift_register_1_q5),
    .q5(shift_register_2_q7[2]), .d6(shift_register_1_q6), .q6(shift_register_2_q7[1]),
    .d7(shift_register_1_q7), .q7(shift_register_2_q7[0]));  // open: in, out, clr
  // DotMatrix #(.inputtype("select"), .matrixcols(8), .matrixrows(8)) dotmatrix_2: pin names not known; wires that end beside it: shift_register_2_q7, Row_Select
  Counter counter_3 (
    .load(PLoad), .count(not_1_out), .Q({counter_3_q, PLoad, Bit_Select}), .clk(CLK));  // open: D, carry, clr
  not not_1 (not_1_out, PLoad);
  Shift_Register shift_register_3 (
    .in(shift_register_1_out), .clk(CLK), .out(shift_register_3_out), .q0(shift_register_3_q0),
    .q1(shift_register_3_q1), .q2(shift_register_3_q2), .q3(shift_register_3_q3), .q4(shift_register_3_q4),
    .q5(shift_register_3_q5), .q6(shift_register_3_q6), .q7(shift_register_3_q7));  // open: shift, load, clr, d0, d1, d2, d3, d4, d5, d6, d7
  Shift_Register shift_register_4 (
    .shift(1'b0), .clk(CLK), .load(PLoad), .d0(shift_register_3_q0), .q0(shift_register_4_q7[7]),
    .d1(shift_register_3_q1), .q1(shift_register_4_q7[6]), .d2(shift_register_3_q2),
    .q2(shift_register_4_q7[5]), .d3(shift_register_3_q3), .q3(shift_register_4_q7[4]),
    .d4(shift_register_3_q4), .q4(shift_register_4_q7[3]), .d5(shift_register_3_q5),
    .q5(shift_register_4_q7[2]), .d6(shift_register_3_q6), .q6(shift_register_4_q7[1]),
    .d7(shift_register_3_q7), .q7(shift_register_4_q7[0]));  // open: in, out, clr
  // DotMatrix #(.inputtype("select"), .matrixcols(8), .matrixrows(8)) dotmatrix_3: pin names not known; wires that end beside it: shift_register_4_q7, Row_Select
  Shift_Register shift_register_5 (
    .in(shift_register_3_out), .clk(CLK), .out(shift_register_5_out), .q0(shift_register_5_q0),
    .q1(shift_register_5_q1), .q2(shift_register_5_q2), .q3(shift_register_5_q3), .q4(shift_register_5_q4),
    .q5(shift_register_5_q5), .q6(shift_register_5_q6), .q7(shift_register_5_q7));  // open: shift, load, clr, d0, d1, d2, d3, d4, d5, d6, d7
  Shift_Register shift_register_6 (
    .shift(1'b0), .clk(CLK), .load(PLoad), .d0(shift_register_5_q0), .q0(shift_register_6_q7[7]),
    .d1(shift_register_5_q1), .q1(shift_register_6_q7[6]), .d2(shift_register_5_q2),
    .q2(shift_register_6_q7[5]), .d3(shift_register_5_q3), .q3(shift_register_6_q7[4]),
    .d4(shift_register_5_q4), .q4(shift_register_6_q7[3]), .d5(shift_register_5_q5),
    .q5(shift_register_6_q7[2]), .d6(shift_register_5_q6), .q6(shift_register_6_q7[1]),
    .d7(shift_register_5_q7), .q7(shift_register_6_q7[0]));  // open: in, out, clr
  // DotMatrix #(.inputtype("select"), .matrixcols(8), .matrixrows(8)) dotmatrix_4: pin names not known; wires that end beside it: shift_register_6_q7, Row_Select
  Shift_Register shift_register_7 (
    .in(shift_register_5_out), .clk(CLK), .q0(shift_register_7_q0), .q1(shift_register_7_q1),
    .q2(shift_register_7_q2), .q3(shift_register_7_q3), .q4(shift_register_7_q4), .q5(shift_register_7_q5),
    .q6(shift_register_7_q6), .q7(shift_register_7_q7));  // open: shift, out, load, clr, d0, d1, d2, d3, d4, d5, d6, d7
  Shift_Register shift_register_8 (
    .shift(1'b0), .clk(CLK), .load(PLoad), .d0(shift_register_7_q0), .q0(shift_register_8_q7[7]),
    .d1(shift_register_7_q1), .q1(shift_register_8_q7[6]), .d2(shift_register_7_q2),
    .q2(shift_register_8_q7[5]), .d3(shift_register_7_q3), .q3(shift_register_8_q7[4]),
    .d4(shift_register_7_q4), .q4(shift_register_8_q7[3]), .d5(shift_register_7_q5),
    .q5(shift_register_8_q7[2]), .d6(shift_register_7_q6), .q6(shift_register_8_q7[1]),
    .d7(shift_register_7_q7), .q7(shift_register_8_q7[0]));  // open: in, out, clr
  // DotMatrix #(.inputtype("select"), .matrixcols(8), .matrixrows(8)) dotmatrix_5: pin names not known; wires that end beside it: shift_register_8_q7, Row_Select

  // Other names for the same wires on the sheet: Bit_Select_ROM[2:0] = Bit_Select[2:0]

  // Notes on the sheet:
  //   contents of rom_1 (hex, n*v repeats v):
  //   fb 9d 9d f5 f5 9d 9d fb
endmodule
